// Logisim project 16bit_datapath.circ as structural Verilog: 6 circuits, main circuit main
module main (
  input  in_1,
  input  Clear,
  output [15:0] out_3,
  output [15:0] Address,
  output [15:0] out_5,
  output [15:0] out_6,
  output [15:0] Read_Data1,
  output [2:0] Read_Reg1,
  output [2:0] WriteReg,
  output [15:0] Data,
  output [15:0] Read_Data2,
  output [2:0] Read_Reg2
);

  wire clock_1_out, clock_2_out, Control_alusrc, Control_memtoreg, Control_reg2loc, Control_regwrite,
       demultiplexer_1_out0, demultiplexer_1_out1, demultiplexer_1_out2, demultiplexer_1_out3,
       demultiplexer_1_out4, demultiplexer_1_out5, demultiplexer_1_out6, demultiplexer_1_out7;
  wire [2:0] xnor_1_out;
  wire [15:0] bit_extender_1_out, multiplexer_2_out, PC_q, R0_q, R1_q, R2_q, R3_q, R4_q, R5_q, R6_q, R7_q;

  Register #(.width(16)) PC (.D(out_3), .en(xnor_1_out[2]), .Q(PC_q), .clk(clock_1_out), .clr(Clear));
  Clock clock_1 (.out(clock_1_out));
  Adder #(.width(16)) adder_1 (.a(16'h1), .b(PC_q), .out(out_3));  // open: cin, cout
  Demultiplexer #(.select(3), .enable("false")) demultiplexer_1 (
    .out0(demultiplexer_1_out0), .out1(demultiplexer_1_out1), .out2(demultiplexer_1_out2),
    .out3(demultiplexer_1_out3), .out4(demultiplexer_1_out4), .out5(demultiplexer_1_out5),
    .out6(demultiplexer_1_out6), .out7(demultiplexer_1_out7), .in(Control_regwrite), .sel(WriteReg));
  ROM #(.addrWidth(16), .dataWidth(16)) rom_1 (.addr(PC_q), .data(out_6), .sel(1'b1));
  Register #(.width(16)) R0 (.D(Data), .en(demultiplexer_1_out0), .Q(R0_q), .clk(clock_1_out));  // open: clr
  Register #(.width(16)) R1 (.D(Data), .en(demultiplexer_1_out1), .Q(R1_q), .clk(clock_1_out));  // open: clr
  Register #(.width(16)) R2 (.D(Data), .en(demultiplexer_1_out2), .Q(R2_q), .clk(clock_1_out));  // open: clr
  Register #(.width(16)) R3 (.D(Data), .en(demultiplexer_1_out3), .Q(R3_q), .clk(clock_1_out));  // open: clr
  Register #(.width(16)) R4 (.D(Data), .en(demultiplexer_1_out4), .Q(R4_q), .clk(clock_1_out));  // open: clr
  Register #(.width(16)) R5 (.D(Data), .en(demultiplexer_1_out5), .Q(R5_q), .clk(clock_1_out));  // open: clr
  Register #(.width(16)) R6 (.D(Data), .en(demultiplexer_1_out6), .Q(R6_q), .clk(clock_1_out));  // open: clr
  Register #(.width(16)) R7 (.D(Data), .en(demultiplexer_1_out7), .Q(R7_q), .clk(clock_1_out));  // open: clr
  Multiplexer #(.width(3), .enable("false")) multiplexer_1 (
    .in0(out_6[2:0]), .in1(out_6[8:6]), .out(WriteReg), .sel(Control_reg2loc));
  Multiplexer #(.width(16), .enable("false")) multiplexer_2 (
    .in0(Read_Data2), .in1(bit_extender_1_out), .out(multiplexer_2_out), .sel(Control_alusrc));
  assign bit_extender_1_out = {{13{1'b0}}, out_6[2:0]};  // Bit_Extender bit_extender_1
  Multiplexer #(.select(3), .width(16), .enable("false")) multiplexer_3 (
    .in0(R0_q), .in1(R1_q), .in2(R2_q), .in3(R3_q), .in4(R4_q), .in5(R5_q), .in6(R6_q), .in7(R7_q),
    .out(Read_Data2), .sel(out_6[5:3]));
  Multiplexer #(.select(3), .width(16), .enable("false")) multiplexer_4 (
    .in0(R0_q), .in1(R1_q), .in2(R2_q), .in3(R3_q), .in4(R4_q), .in5(R5_q), .in6(R6_q), .in7(R7_q),
    .out(Read_Data1), .sel(out_6[8:6]));
  ALU ALU (.Input1(Read_Data1), .Input2(multiplexer_2_out), .ALUOp(out_6[10:9]), .Output(Address));
  Control Control (
    .Command(out_6[10:9]), .ALUSrc(Control_alusrc), .RegWrite(Control_regwrite), .MemToReg(Control_memtoreg),
    .Reg2Loc(Control_reg2loc));  // open: MemRead, MemWrite
  Clock clock_2 (.out(clock_2_out));
  Multiplexer #(.width(16), .enable("false")) multiplexer_5 (
    .in0(Address), .in1(out_5), .out(Data), .sel(Control_memtoreg));
  assign xnor_1_out = ~(out_6[8:6] ^ out_6[5:3]);  // XNOR_Gate xnor_1, 3 bits wide
  RAM #(.addrWidth(16), .dataWidth(16), .bus("separate")) ram_1 (
    .addr(Address), .data(out_5), .str(xnor_1_out[0]), .sel(1'b1), .clk(clock_2_out), .ld(xnor_1_out[1]),
    .clr(in_1));  // open: din

  assign Read_Reg1 = out_6[8:6];
  assign Read_Reg2 = out_6[5:3];

  // Notes on the sheet:
  //   contents of rom_1 (hex, n*v repeats v):
  //   440 481 53 254
endmodule

module PC (
  input  En,
  input  Clear,
  output [15:0] out_3,
  output [15:0] out_4
);

  wire clock_1_out;
  wire [15:0] PC_q;

  Register #(.width(16)) PC (.D(out_3), .en(En), .Q(PC_q), .clk(clock_1_out), .clr(Clear));
  Clock clock_1 (.out(clock_1_out));
  Adder #(.width(16)) adder_1 (.a(16'h1), .b(PC_q), .out(out_3));  // open: cin, cout
  ROM #(.addrWidth(16), .dataWidth(16)) rom_1 (.addr(PC_q), .data(out_4), .sel(1'b1));

  // Notes on the sheet:
  //   contents of rom_1 (hex, n*v repeats v):
  //   12 1234 ed23 34ae
endmodule

module ALU (
  input  [15:0] Input1,
  input  [15:0] Input2,
  input  [1:0] ALUOp,
  output [15:0] Output
);

  wire [15:0] adder_1_out, AND_out;

  Adder #(.width(16)) adder_1 (.a(Input1), .b(Input2), .out(adder_1_out));  // open: cin, cout
  assign AND_out = Input1 & Input2;  // AND_Gate AND, 16 bits wide
  Multiplexer #(.select(2), .width(16), .enable("false")) multiplexer_1 (
    .in0(adder_1_out), .in1(AND_out), .in2(adder_1_out), .out(Output), .sel(ALUOp));  // open: in3
endmodule

module MEM (
  input  [15:0] Address,
  input  [15:0] WriteData,
  input  in_3,
  input  MemWrite,
  input  MemRead,
  output [15:0] out_6
);

  wire clock_1_out;

  Clock clock_1 (.out(clock_1_out));
  RAM #(.addrWidth(16), .dataWidth(16), .bus("separate")) ram_1 (
    .addr(Address), .din(WriteData), .data(out_6), .str(MemWrite), .sel(1'b1), .clk(clock_1_out),
    .ld(MemRead), .clr(in_3));
endmodule

module \Regşsters  (
  input  in_1,
  input  [2:0] Read_Reg1,
  input  [2:0] WriteReg,
  input  [15:0] Data,
  input  [2:0] Read_Reg2,
  output [15:0] Read_Data1,
  output [15:0] Read_Data2
);

  wire clock_1_out, demultiplexer_1_out0, demultiplexer_1_out1, demultiplexer_1_out2, demultiplexer_1_out3,
       demultiplexer_1_out4, demultiplexer_1_out5, demultiplexer_1_out6, demultiplexer_1_out7;
  wire [15:0] register_1_q, register_2_q, register_3_q, register_4_q, register_5_q, register_6_q,
       register_7_q, register_8_q;

  Demultiplexer #(.select(3), .enable("false")) demultiplexer_1 (
    .out0(demultiplexer_1_out0), .out1(demultiplexer_1_out1), .out2(demultiplexer_1_out2),
    .out3(demultiplexer_1_out3), .out4(demultiplexer_1_out4), .out5(demultiplexer_1_out5),
    .out6(demultiplexer_1_out6), .out7(demultiplexer_1_out7), .in(in_1), .sel(WriteReg));
  Clock clock_1 (.out(clock_1_out));
  Register #(.width(16)) register_1 (
    .D(Data), .en(demultiplexer_1_out0), .Q(register_1_q), .clk(clock_1_out));  // open: clr
  Register #(.width(16)) register_2 (
    .D(Data), .en(demultiplexer_1_out1), .Q(register_2_q), .clk(clock_1_out));  // open: clr
  Register #(.width(16)) register_3 (
    .D(Data), .en(demultiplexer_1_out2), .Q(register_3_q), .clk(clock_1_out));  // open: clr
  Register #(.width(16)) register_4 (
    .D(Data), .en(demultiplexer_1_out3), .Q(register_4_q), .clk(clock_1_out));  // open: clr
  Register #(.width(16)) register_5 (
    .D(Data), .en(demultiplexer_1_out4), .Q(register_5_q), .clk(clock_1_out));  // open: clr
  Register #(.width(16)) register_6 (
    .D(Data), .en(demultiplexer_1_out5), .Q(register_6_q), .clk(clock_1_out));  // open: clr
  Register #(.width(16)) register_7 (
    .D(Data), .en(demultiplexer_1_out6), .Q(register_7_q), .clk(clock_1_out));  // open: clr
  Register #(.width(16)) register_8 (
    .D(Data), .en(demultiplexer_1_out7), .Q(register_8_q), .clk(clock_1_out));  // open: clr
  Multiplexer #(.select(3), .width(16), .enable("false")) multiplexer_1 (
    .in0(register_1_q), .in1(register_2_q), .in2(register_3_q), .in3(register_4_q), .in4(register_5_q),
    .in5(register_6_q), .in6(register_7_q), .in7(register_8_q), .out(Read_Data2), .sel(Read_Reg2));
  Multiplexer #(.select(3), .width(16), .enable("false")) multiplexer_2 (
    .in0(register_1_q), .in1(register_2_q), .in2(register_3_q), .in3(register_4_q), .in4(register_5_q),
    .in5(register_6_q), .in6(register_7_q), .in7(register_8_q), .out(Read_Data1), .sel(Read_Reg1));
endmodule

module Control (
  input  [1:0] Command,
  output MemRead,
  output MemWrite,
  output ALUSrc,
  output RegWrite,
  output MemToReg,
  output Reg2Loc
);

  wire not_1_out;

  not not_1 (not_1_out, Command[0]);
  and and_1 (ALUSrc, not_1_out, Command[1]);
  or or_1 (RegWrite, ALUSrc, 1'b1);
  not not_2 (MemWrite, ALUSrc);

  assign MemRead = ALUSrc;
  assign MemToReg = ALUSrc;
  assign Reg2Loc = ALUSrc;
endmodule
